// Logisim project GeneradorPixeles.circ as structural Verilog: 1 circuit, main circuit GeneradorPixeles
module GeneradorPixeles (
  input  Reset,
  input  Start,
  input  Clock,
  output [3:0] X,
  output [3:0] Y
);

  wire contadorx_1_carry;

  contadorX contadorx_1 (.Reset(Reset), .Start(Start), .Clock(Clock), .Carry(contadorx_1_carry), .X(X));
  contadorY contadory_1 (.Reset(Reset), .Start(contadorx_1_carry), .Clock(Clock), .Y(Y));  // open: Carry
endmodule
