// Logisim project intentodeCalculoF.circ as structural Verilog: 1 circuit, main circuit main
module main (
  input  [3:0] A,
  input  [3:0] B,
  input  [3:0] C,
  input  [3:0] Y
);

  wire and_1_out, Clock, d_ff_1_qn, Reset;
  wire [15:0] F_in, F_out, F_row_in_R, F_row_in_T, F_row_out;

  Clock Clk (.out(Clock));
  Button button_1 (.out(Reset));
  CarrySkipAdder carryskipadder_1 (.A(F_out), .B({{13{A[3]}}, A[2:0]}), .S(F_in));  // open: C_in, C_out
  CarrySkipAdder carryskipadder_2 (.A(F_row_out), .B({{13{B[3]}}, B[2:0]}), .S(F_row_in_T));  // open: C_in, C_out
  D_Flip_Flop d_ff_1 (.D(1'b1), .clk(Clock), .Qn(d_ff_1_qn), .reset(Reset));  // open: Q, preset
  Register #(.width(16)) F (.D(F_in), .clk(Clock), .Q(F_out), .clr(Reset));  // open: en
  Register #(.width(16)) F_row (.D(F_row_in_R), .clk(Clock), .Q(F_row_out), .clr(Reset));  // open: en
  Multiplexer #(.width(16)) multiplexer_1 (
    .in0(F_row_in_T), .in1({{13{C[3]}}, C[2:0]}), .out(F_row_in_R), .sel(and_1_out));
  and and_1 (and_1_out, d_ff_1_qn, 1'b1);
endmodule
